# Fritzing sketch Circuito (saved by Fritzing 0.9.3b)
breadboards: 1

parts:
  U1 = ESP8266 WiFi Module [part_number=ESP8266]
  1_Channel_Relay1 = 1 Channel Power Relay  # not connected
  RHT1 = Humidity and Temperature Sensor RHT03
  U4 = CP2102 USB Module

nets:
  N1: U1.IO4, RHT1.Data-signal
  N2: U1.3.3V#10, RHT1.Vcc
  N3: U1.3.3V#11, U1.CHIP_EN, U4.3V3
  N4: U1.GND#12, U1.IO15, U4.GND
  N5: U1.GND#13, RHT1.GND_2
  N6: U1.TX, U4.RXD
  N7: U1.RX, U4.TXD

custom parts:
  1 Channel Power Relay: A 1 channel power relay. The module operates at 5V.
  CP2102 USB Module: 6Pin USB 2.0 to TTL UART Module Serial Converter CP2102 STC Replace Ft232 Module
