# Fritzing sketch Circuit_pc (saved by Fritzing 0.9.3b)
breadboards: 1

parts:
  U1 = ESP8266 WiFi Module [part_number=ESP8266]
  RHT1 = Humidity and Temperature Sensor RHT03
  U4 = CP2102 USB Module
  R1 = Resistor [tolerance=±5% resistance=220 package=THT]
  KY-1 = Keyes Relay [package=THT]

nets:
  N1: U1.IO0, U1.D2, U1.GND#12, U1.IO12, U1.IO15, U4.GND, KY-1.ground
  N2: U1.IO4, RHT1.Data-signal, R1.Pin_1
  N3: U1.3.3V#10, RHT1.Vcc, R1.Pin_0
  N4: U1.3.3V#11, U1.CHIP_EN, U4.3V3, KY-1.signal
  N5: U1.GND#13, RHT1.GND_2
  N6: U1.IO5, KY-1.power
  N7: U1.T_OUT, U1.RST, U1.XPD
  N8: U1.TX, U4.RXD
  N9: U1.RX, U4.TXD

custom parts:
  CP2102 USB Module: 6Pin USB 2.0 to TTL UART Module Serial Converter CP2102 STC Replace Ft232 Module
  Keyes Relay: The Keyes 5V relay module is suitable for SCM development, home appliance control. It uses a 5V~12V TIL control signal which can control DC / AC signal.
